// Digital circuit 1X15 SRAM.dig as structural Verilog
module _1X15_SRAM (
  input  RS1,
  input  RS2,
  input  CLK,
  input  WS,
  input  [14:0] WD_14_0,
  output [14:0] RD1,
  output [14:0] RD2
);

  _1X1_SRAM _1x1_sram_1 (.WD(WD_14_0[0]), .WS(WS), .RS1(RS1), .RS2(RS2), .CLK(CLK), .RD1(RD1[0]), .RD2(RD2[0]));
  _1X1_SRAM _1x1_sram_2 (.WD(WD_14_0[5]), .WS(WS), .RS1(RS1), .RS2(RS2), .CLK(CLK), .RD1(RD1[5]), .RD2(RD2[5]));
  _1X1_SRAM _1x1_sram_3 (.WD(WD_14_0[10]), .WS(WS), .RS1(RS1), .RS2(RS2), .CLK(CLK), .RD1(RD1[10]), .RD2(RD2[10]));
  _1X1_SRAM _1x1_sram_4 (.WD(WD_14_0[1]), .WS(WS), .RS1(RS1), .RS2(RS2), .CLK(CLK), .RD1(RD1[1]), .RD2(RD2[1]));
  _1X1_SRAM _1x1_sram_5 (.WD(WD_14_0[6]), .WS(WS), .RS1(RS1), .RS2(RS2), .CLK(CLK), .RD1(RD1[6]), .RD2(RD2[6]));
  _1X1_SRAM _1x1_sram_6 (.WD(WD_14_0[11]), .WS(WS), .RS1(RS1), .RS2(RS2), .CLK(CLK), .RD1(RD1[11]), .RD2(RD2[11]));
  _1X1_SRAM _1x1_sram_7 (.WD(WD_14_0[2]), .WS(WS), .RS1(RS1), .RS2(RS2), .CLK(CLK), .RD1(RD1[2]), .RD2(RD2[2]));
  _1X1_SRAM _1x1_sram_8 (.WD(WD_14_0[7]), .WS(WS), .RS1(RS1), .RS2(RS2), .CLK(CLK), .RD1(RD1[7]), .RD2(RD2[7]));
  _1X1_SRAM _1x1_sram_9 (.WD(WD_14_0[12]), .WS(WS), .RS1(RS1), .RS2(RS2), .CLK(CLK), .RD1(RD1[12]), .RD2(RD2[12]));
  _1X1_SRAM _1x1_sram_10 (.WD(WD_14_0[3]), .WS(WS), .RS1(RS1), .RS2(RS2), .CLK(CLK), .RD1(RD1[3]), .RD2(RD2[3]));
  _1X1_SRAM _1x1_sram_11 (.WD(WD_14_0[8]), .WS(WS), .RS1(RS1), .RS2(RS2), .CLK(CLK), .RD1(RD1[8]), .RD2(RD2[8]));
  _1X1_SRAM _1x1_sram_12 (.WD(WD_14_0[13]), .WS(WS), .RS1(RS1), .RS2(RS2), .CLK(CLK), .RD1(RD1[13]), .RD2(RD2[13]));
  _1X1_SRAM _1x1_sram_13 (.WD(WD_14_0[4]), .WS(WS), .RS1(RS1), .RS2(RS2), .CLK(CLK), .RD1(RD1[4]), .RD2(RD2[4]));
  _1X1_SRAM _1x1_sram_14 (.WD(WD_14_0[9]), .WS(WS), .RS1(RS1), .RS2(RS2), .CLK(CLK), .RD1(RD1[9]), .RD2(RD2[9]));
  _1X1_SRAM _1x1_sram_15 (.WD(WD_14_0[14]), .WS(WS), .RS1(RS1), .RS2(RS2), .CLK(CLK), .RD1(RD1[14]), .RD2(RD2[14]));

  // Other names for the same wires on the sheet: RD2_0 = RD2[0]; RD2_1 = RD2[1]; RD2_2 = RD2[2]; RD2_3 = RD2[3];
  //   RD2_4 = RD2[4]; RD2_5 = RD2[5]; RD2_6 = RD2[6]; RD2_7 = RD2[7]; RD2_8 = RD2[8]; RD2_9 = RD2[9];
  //   RD2_10 = RD2[10]; RD2_11 = RD2[11]; RD2_12 = RD2[12]; RD2_13 = RD2[13]; RD2_14 = RD2[14]; RD_0 = RD1[0];
  //   RD_1 = RD1[1]; RD_2 = RD1[2]; RD_3 = RD1[3]; RD_4 = RD1[4]; RD_5 = RD1[5]; RD_6 = RD1[6]; RD_7 = RD1[7];
  //   RD_8 = RD1[8]; RD_9 = RD1[9]; RD_10 = RD1[10]; RD_11 = RD1[11]; RD_12 = RD1[12]; RD_13 = RD1[13];
  //   RD_14 = RD1[14]; WD_0 = WD_14_0[0]; WD_1 = WD_14_0[1]; WD_2 = WD_14_0[2]; WD_3 = WD_14_0[3]; WD_4 = WD_14_0[4];
  //   WD_5 = WD_14_0[5]; WD_6 = WD_14_0[6]; WD_7 = WD_14_0[7]; WD_8 = WD_14_0[8]; WD_9 = WD_14_0[9];
  //   WD_10 = WD_14_0[10]; WD_11 = WD_14_0[11]; WD_12 = WD_14_0[12]; WD_13 = WD_14_0[13]; WD_14 = WD_14_0[14]
endmodule
