// Digital circuit 3bit Register.dig as structural Verilog
module _3bit_Register (
  input  [2:0] Din_2_0,
  input  Sel,
  input  CLK,
  output [2:0] Dout_2_0
);

  _1bit_Register _1bit_register_1 (.Dout(Dout_2_0[0]), .Din(Din_2_0[0]), .Sel(Sel), .CLK(CLK));
  _1bit_Register _1bit_register_2 (.Dout(Dout_2_0[1]), .Din(Din_2_0[1]), .Sel(Sel), .CLK(CLK));
  _1bit_Register _1bit_register_3 (.Dout(Dout_2_0[2]), .Din(Din_2_0[2]), .Sel(Sel), .CLK(CLK));

  // Other names for the same wires on the sheet: Din0 = Din_2_0[0]; Din1 = Din_2_0[1]; Din2 = Din_2_0[2];
  //   Dout0 = Dout_2_0[0]; Dout1 = Dout_2_0[1]; Dout2 = Dout_2_0[2]
endmodule
