// Digital circuit 4bit Register.dig as structural Verilog
module _4bit_Register (
  input  [3:0] Din_3_0,
  input  Sel,
  input  CLK,
  output [3:0] Dout_3_0
);

  _1bit_Register _1bit_register_1 (.Dout(Dout_3_0[0]), .Din(Din_3_0[0]), .Sel(Sel), .CLK(CLK));
  _1bit_Register _1bit_register_2 (.Dout(Dout_3_0[1]), .Din(Din_3_0[1]), .Sel(Sel), .CLK(CLK));
  _1bit_Register _1bit_register_3 (.Dout(Dout_3_0[2]), .Din(Din_3_0[2]), .Sel(Sel), .CLK(CLK));
  _1bit_Register _1bit_register_4 (.Dout(Dout_3_0[3]), .Din(Din_3_0[3]), .Sel(Sel), .CLK(CLK));

  // Other names for the same wires on the sheet: Din0 = Din_3_0[0]; Din1 = Din_3_0[1]; Din2 = Din_3_0[2];
  //   Din3 = Din_3_0[3]; Dout0 = Dout_3_0[0]; Dout1 = Dout_3_0[1]; Dout2 = Dout_3_0[2]; Dout3 = Dout_3_0[3]
endmodule
