// Digital circuit 4bitAdder.dig as structural Verilog
module _4bitAdder (
  input  [3:0] A_3_0,
  input  [3:0] B_3_0,
  output [3:0] R_3_0,
  output Cout
);

  wire fa_2_cout, fa_3_cout, fa_4_cout;

  FA fa_1 (.x(A_3_0[3]), .y(B_3_0[3]), .Cin(fa_2_cout), .Cout(Cout), .S(R_3_0[3]));
  FA fa_2 (.x(A_3_0[2]), .y(B_3_0[2]), .Cin(fa_3_cout), .Cout(fa_2_cout), .S(R_3_0[2]));
  FA fa_3 (.x(A_3_0[1]), .y(B_3_0[1]), .Cin(fa_4_cout), .Cout(fa_3_cout), .S(R_3_0[1]));
  FA fa_4 (.x(A_3_0[0]), .y(B_3_0[0]), .Cin(1'b0), .Cout(fa_4_cout), .S(R_3_0[0]));
endmodule
