// Digital circuit 7X15 SRAM.dig as structural Verilog
module _7X15_SRAM (
  input  [2:0] RA1_2_0,
  input  [2:0] RA2_2_0,
  input  [2:0] WR_2_0,
  input  [14:0] WRD_14_0,
  input  CLK,
  input  WE,
  output [14:0] RD1_14_0,
  output [14:0] RD2_14_0
);

  wire RA1_0, RA1_1, RA1_2, RA1_3, RA1_4, RA1_5, RA1_6, RA1_7, RA2_0, RA2_1, RA2_2, RA2_3, RA2_4, RA2_5,
       RA2_6, RA2_7, W_0, W_1, W_2, W_3, W_4, W_5, W_6, W_7, WS_0, WS_1, WS_2, WS_3, WS_4, WS_5, WS_6;
  wire [14:0] or_1_out, or_2_out, or_3_out, or_4_out, RD1_0, RD1_1, RD1_2, RD1_3, RD1_4, RD1_5, RD1_6, RD2_0,
       RD2_1, RD2_2, RD2_3, RD2_4, RD2_5, RD2_6;

  Decoder #(.Selector_Bits(3)) decoder_1 (
    .sel(RA1_2_0), .out_0(RA1_0), .out_1(RA1_1), .out_2(RA1_2), .out_3(RA1_3), .out_4(RA1_4), .out_5(RA1_5),
    .out_6(RA1_6), .out_7(RA1_7));
  Decoder #(.Selector_Bits(3)) decoder_2 (
    .sel(RA2_2_0), .out_0(RA2_0), .out_1(RA2_1), .out_2(RA2_2), .out_3(RA2_3), .out_4(RA2_4), .out_5(RA2_5),
    .out_6(RA2_6), .out_7(RA2_7));
  Decoder #(.Selector_Bits(3)) decoder_3 (
    .sel(WR_2_0), .out_0(W_0), .out_1(W_1), .out_2(W_2), .out_3(W_3), .out_4(W_4), .out_5(W_5), .out_6(W_6),
    .out_7(W_7));
  and and_1 (WS_0, W_0, WE);
  and and_2 (WS_1, W_1, WE);
  and and_3 (WS_2, W_2, WE);
  and and_4 (WS_3, W_3, WE);
  and and_5 (WS_4, W_4, WE);
  and and_6 (WS_5, W_5, WE);
  and and_7 (WS_6, W_6, WE);
  _1X15_SRAM _1x15_sram_1 (
    .RS1(RA1_0), .RS2(RA2_0), .WS(WS_0), .WD_14_0(WRD_14_0), .CLK(CLK), .RD1(RD1_0), .RD2(RD2_0));
  _1X15_SRAM _1x15_sram_2 (
    .RS1(RA1_1), .RS2(RA2_1), .WS(WS_1), .WD_14_0(WRD_14_0), .CLK(CLK), .RD1(RD1_1), .RD2(RD2_1));
  _1X15_SRAM _1x15_sram_3 (
    .RS1(RA1_2), .RS2(RA2_2), .WS(WS_2), .WD_14_0(WRD_14_0), .CLK(CLK), .RD1(RD1_2), .RD2(RD2_2));
  _1X15_SRAM _1x15_sram_4 (
    .RS1(RA1_3), .RS2(RA2_3), .WS(WS_3), .WD_14_0(WRD_14_0), .CLK(CLK), .RD1(RD1_3), .RD2(RD2_3));
  _1X15_SRAM _1x15_sram_5 (
    .RS1(RA1_4), .RS2(RA2_4), .WS(WS_4), .WD_14_0(WRD_14_0), .CLK(CLK), .RD1(RD1_4), .RD2(RD2_4));
  _1X15_SRAM _1x15_sram_6 (
    .RS1(RA1_5), .RS2(RA2_5), .WS(WS_5), .WD_14_0(WRD_14_0), .CLK(CLK), .RD1(RD1_5), .RD2(RD2_5));
  _1X15_SRAM _1x15_sram_7 (
    .RS1(RA1_6), .RS2(RA2_6), .WS(WS_6), .WD_14_0(WRD_14_0), .CLK(CLK), .RD1(RD1_6), .RD2(RD2_6));
  assign or_1_out = RD1_0 | RD1_1 | RD1_2 | RD1_3 | RD1_4;  // Or or_1, 15 bits wide
  assign or_2_out = RD1_5 | RD1_6;  // Or or_2, 15 bits wide
  assign or_3_out = RD2_0 | RD2_1 | RD2_2 | RD2_3 | RD2_4;  // Or or_3, 15 bits wide
  assign or_4_out = RD2_5 | RD2_6;  // Or or_4, 15 bits wide
  assign RD1_14_0 = or_1_out | or_2_out;  // Or or_5, 15 bits wide
  assign RD2_14_0 = or_3_out | or_4_out;  // Or or_6, 15 bits wide

  // Other names for the same wires on the sheet: RA1[2:0] = RA1_2_0; RA2[2:0] = RA2_2_0; WR[2:0] = WR_2_0
endmodule
