// Digital circuit CPU(main).dig as structural Verilog
module CPU_main (
  input  [2:0] WR_2_0,
  input  [14:0] WRD_14_0,
  input  CLK,
  input  WE,
  input  PC_EN,
  input  [2:0] RA2_2_0,
  input  ZF,
  input  SF,
  output [14:0] RD1_14_0,
  output [14:0] RD2_14_0,
  output [3:0] out_9,
  output [3:0] out_10,
  output [3:0] out_11,
  output [1:0] out_12,
  output [3:0] out_13
);

  wire CPU_CLK, Imm_sel, JMP_Sel, Reg_EN;
  wire [2:0] _3_bit_Adder_o_2_0, _3bit_PC_o_2_0, multiplexer_1_out;
  wire [3:0] B_3_0;

  Multiplexer #(.Bits(3)) multiplexer_1 (
    .sel(JMP_Sel), .in_0(_3_bit_Adder_o_2_0), .in_1({RD1_14_0[10:9], out_13[3]}), .out(multiplexer_1_out));
  Program_Counter _3bit_PC (.I_2_0(multiplexer_1_out), .CLK(CPU_CLK), .O_2_0(_3bit_PC_o_2_0));
  AddOne_Circuit _3_bit_Adder (.I_2_0(_3bit_PC_o_2_0), .O_2_0(_3_bit_Adder_o_2_0));
  and and_1 (CPU_CLK, PC_EN, CLK);
  _7X15_SRAM _7x15_sram_1 (
    .RA1_2_0(_3bit_PC_o_2_0), .RA2_2_0(RA2_2_0), .WR_2_0(WR_2_0), .WRD_14_0(WRD_14_0), .WE(WE), .CLK(CLK),
    .RD1_14_0({RD1_14_0[14:9], out_13, RD1_14_0[4:0]}), .RD2_14_0(RD2_14_0));
  _4bit_register_set _4bit_register_set_1 (
    .WR_1_0(RD1_14_0[10:9]), .CLK(CPU_CLK), .WE(Reg_EN), .WRD_3_0(out_9), .RA_1_0(RD1_14_0[10:9]),
    .RB_1_0(out_13[3:2]), .A_3_0(out_10), .B_3_0(B_3_0));
  _4bit_ALU _4bit_alu_1 (.A_3_0(out_10), .B_3_0(out_11), .R_3_0(out_9), .OP_1_0(out_12));
  control_unit control_unit_1 (
    .OPCODE_3_0(RD1_14_0[14:11]), .ZF(ZF), .SF(SF), .OP_1_0(out_12), .Reg_EN(Reg_EN), .Imm_sel(Imm_sel),
    .JMP_Sel(JMP_Sel));
  Multiplexer #(.Bits(4)) multiplexer_2 (.sel(Imm_sel), .in_0(B_3_0), .in_1(out_13), .out(out_11));

  assign RD1_14_0[8:5] = out_13;

  // Other names for the same wires on the sheet: A_3_0[3:0] = out_10; B1_3_0[3:0] = out_11; OP_1_0[1:0] = out_12;
  //   RA2[2:0] = RA2_2_0; Don_t_Care[6:0] = {out_13[1:0], RD1_14_0[4:0]};
  //   RD1[14:0] = {RD1_14_0[14:9], out_13, RD1_14_0[4:0]}; Const[3:0] = out_13; R2[1:0] = out_13[3:2];
  //   JMP_Add[2:0] = {RD1_14_0[10:9], out_13[3]}; R1[1:0] = RD1_14_0[10:9]; OP_3_0[3:0] = RD1_14_0[14:11];
  //   RD2[14:0] = RD2_14_0; Result_3_0[3:0] = out_9

  // Notes on the sheet:
  //   Register Mode : 2 bit (type of OP=00) + 2 bit OP + 2 bit (Ra) + 2 bit (Rb) + 7 bit (Don't care) | Total 15 bit
  //   Immediate Mode : 2 bit (type of OP=01) + 2 bit OP + 2 bit (Ra) + 4 bit (Rb) +5  bit (Don't care) | Total 15 bit
  //   XOR (OP = 01), ADD (OP = 10), ROR (OP = 00)
  //   JMP Mode : 2 bit (type of OP=10) + 2 bit OP + 3 bit (Ra)
  //   JMP (OP=00), JG (OP=01)
  //   0 XOR R0,R0 -> 0b000100000000000
  //   1 XOR R1,R1 -> 0b000101010000000
  //   2 JMP REPEAT-> 0b100011000000000
  //   3 START:
  //     ADD R0,01 -> 0b011000000100000
  //   4 ADD R1,06 -> 0b011001011000000
  //   5 ROR R1,R0 -> 0b000001000000000
  //   6 REPEAT:
  //     JG START  -> 0b100101100000000
endmodule
