// Digital circuit Program Counter.dig as structural Verilog
module Program_Counter (
  input  [2:0] I_2_0,
  input  CLK,
  output [2:0] O_2_0
);

  _3bit_Register _3bit_register_1 (.Din_2_0(I_2_0), .Sel(1'b1), .CLK(CLK), .Dout_2_0(O_2_0));
endmodule
