// Digital circuit control unit.dig as structural Verilog
module control_unit (
  input  [3:0] OPCODE_3_0,
  input  ZF,
  input  SF,
  output [1:0] OP_1_0,
  output Reg_EN,
  output Imm_sel,
  output JMP_Sel
);

  wire and_1_out, and_3_out, and_4_out, and_5_out, or_2_out;

  and and_1 (and_1_out, ~OPCODE_3_0[2], ~OPCODE_3_0[3]);  // And
  and and_2 (Imm_sel, OPCODE_3_0[2], ~OPCODE_3_0[3]);  // And
  and and_3 (and_3_out, ~OPCODE_3_0[2], OPCODE_3_0[3]);  // And
  and and_4 (and_4_out, ~OPCODE_3_0[0], ~OPCODE_3_0[1]);  // And
  and and_5 (and_5_out, OPCODE_3_0[0], ~OPCODE_3_0[1], ~ZF, ~SF);  // And
  or or_1 (Reg_EN, and_1_out, Imm_sel);
  or or_2 (or_2_out, and_4_out, and_5_out);
  and and_6 (JMP_Sel, and_3_out, or_2_out);

  assign OP_1_0 = OPCODE_3_0[1:0];
endmodule
